# Fritzing sketch splitski_sat_v02 (saved by Fritzing 0.9.2b)
circuit board: 8.46667cm x 5.64444cm
breadboards: 1

parts:
  Arduino_Nano_V3_0 = Arduino Nano (Rev3.0)
  S1 = Pushbutton [package="[THT]"]
  S2 = Pushbutton [package="[THT]"]
  S3 = Pushbutton [package="[THT]"]
  S4 = Pushbutton [package="[THT]"]
  Tiny_RTC1 = Tiny RTC
  J1 = double row female pin header, 16 pins [form="♀ (female)"]
  J2 = female pin header, 2 pins [form="♀ (female)"]

nets:
  N1: Arduino_Nano_V3_0.GND, S1.Pin_1, S1.Pin_2, S2.Pin_1, S2.Pin_2, S3.Pin_1, S3.Pin_2, S4.Pin_1, S4.Pin_2, Tiny_RTC1.GND#4, J1.pin8, J2.pin1
  N2: Arduino_Nano_V3_0.D4, J1.pin16
  N3: Arduino_Nano_V3_0.D5, J1.pin15
  N4: Arduino_Nano_V3_0.D6, J1.pin14
  N5: Arduino_Nano_V3_0.D7, J1.pin13
  N6: Arduino_Nano_V3_0.D8, J1.pin4
  N7: Arduino_Nano_V3_0.D9, J1.pin5
  N8: Arduino_Nano_V3_0.D10, J1.pin10
  N9: Arduino_Nano_V3_0.D11/MOSI, J1.pin9
  N10: Arduino_Nano_V3_0.5V, Tiny_RTC1.VCC#3, J2.pin2
  N11: Arduino_Nano_V3_0.A5, Tiny_RTC1.SCL#1
  N12: Arduino_Nano_V3_0.A4, Tiny_RTC1.SDA#2
  N13: Arduino_Nano_V3_0.A3, S4.Pin_3, S4.Pin_4
  N14: Arduino_Nano_V3_0.A2, S3.Pin_3, S3.Pin_4
  N15: Arduino_Nano_V3_0.A1, S2.Pin_3, S2.Pin_4
  N16: Arduino_Nano_V3_0.A0, S1.Pin_3, S1.Pin_4

custom parts:
  Tiny RTC: Tiny RTC I2C module DS1370Z RTC and AT24C32 EEPROM
